// Logisim project calculator.circ as structural Verilog: 1 circuit, main circuit main
module main (
  input  Input_1,
  input  Input_2,
  input  Input_3,
  input  Input_4,
  output [12:0] out_5
);

  wire AddrEn, AEn, BEn, Button_1_out, Button_2_out, CEn, CLEAR, Clk, controlled_buffer_1_out,
       controlled_buffer_2_out, CoordEn, or_1_out, Q0, Q1, Q2;
  wire [2:0] CURRENT_STATE_eb77bd12;
  wire [3:0] controlled_buffer_3_out, controlled_buffer_5_out, controlled_buffer_6_out;
  wire [9:8] ROM_1_data;

  Clock clock_1 (.out(Clk));
  Button Button_1 (.out(Button_1_out));
  Button Button_2 (.out(Button_2_out));
  assign controlled_buffer_1_out = Button_1_out ? 1'b0 : 1'bz;  // Controlled_Buffer controlled_buffer_1
  assign controlled_buffer_2_out = Button_2_out ? 1'b1 : 1'bz;  // Controlled_Buffer controlled_buffer_2
  Register #(.width(3)) register_1 (.D({Q2, Q1, Q0}), .Q(CURRENT_STATE_eb77bd12), .clk(Clk));  // open: en, clr
  assign controlled_buffer_3_out = AEn ? {Input_4, Input_3, Input_2, Input_1} : 4'bz;  // Controlled_Buffer controlled_buffer_3
  assign CLEAR = or_1_out ? controlled_buffer_2_out : 1'bz;  // Controlled_Buffer controlled_buffer_4
  or or_1 (or_1_out, CURRENT_STATE_eb77bd12[0], CURRENT_STATE_eb77bd12[1], CURRENT_STATE_eb77bd12[2]);
  assign controlled_buffer_5_out = BEn ? {Input_4, Input_3, Input_2, Input_1} : 4'bz;  // Controlled_Buffer controlled_buffer_5
  assign controlled_buffer_6_out = CEn ? {Input_4, Input_3, Input_2, Input_1} : 4'bz;  // Controlled_Buffer controlled_buffer_6
  Register #(.width(1)) Coordinate_System_eac7d053 (
    .D(controlled_buffer_1_out), .en(CoordEn), .Q(out_5[0]), .clk(Clk), .clr(CLEAR));
  ROM #(.addrWidth(3), .dataWidth(10)) ROM_1 (
    .addr(CURRENT_STATE_eb77bd12), .data({ROM_1_data, CoordEn, AEn, BEn, CEn, AddrEn, Q2, Q1, Q0}));
  Register #(.width(4)) CoefficientA (.D(controlled_buffer_3_out), .en(1'b1), .Q(out_5[4:1]), .clk(Clk), .clr(CLEAR));
  Register #(.width(4)) CoefficientB (.D(controlled_buffer_5_out), .en(1'b1), .Q(out_5[8:5]), .clk(Clk), .clr(CLEAR));
  Register #(.width(4)) CoefficientC (.D(controlled_buffer_6_out), .en(1'b1), .Q(out_5[12:9]), .clk(Clk), .clr(CLEAR));
  LED Led2 (.in(ROM_1_data[8]));
  LED Led1 (.in(ROM_1_data[9]));

  // Notes on the sheet:
  //   Clear/Rectangular
  //   Switches
  //   Polar
  //   contents of ROM_1 (hex, n*v repeats v):
  //   81 42 23 14 108
endmodule
